// Logisim project processador.circ as structural Verilog: 5 circuits, main circuit main
module main (
);

  wire ALUSrc, Branch, clock_1_out, Jump, MemToReg, MemWrite, ula_1_zero, WriteR0, WriteReg;
  wire [1:0] multiplexer_3_out;
  wire [1:1] and_1_out;
  wire [2:0] ALUOp;
  wire [3:0] Opcode, Resto;
  wire [7:0] adder_1_out, adder_2_out, bancoderegistradores_1_a, bancoderegistradores_1_b,
       dual_port_ram_1_data, extensorsinal_1_b, extensorsinal_2_b, multiplexer_1_out, multiplexer_2_out,
       multiplexer_4_out, register_1_q, ula_1_s;

  and and_1 (and_1_out[1], Branch, ula_1_zero);
  ExtensorSinal extensorsinal_1 (.A(Resto), .B(extensorsinal_1_b));
  Adder adder_1 (.a(extensorsinal_1_b), .b(register_1_q), .out(adder_1_out));  // open: cin, cout
  // Probe on adder_1_out
  // Probe on adder_2_out
  Adder adder_2 (.a(8'h1), .b(register_1_q), .out(adder_2_out));  // open: cin, cout
  Multiplexer #(.select(2), .width(8)) multiplexer_1 (
    .in0(adder_2_out), .in1(adder_1_out), .in2(bancoderegistradores_1_b), .out(multiplexer_1_out),
    .sel({and_1_out[1], Jump}));  // open: in3
  // Probe on multiplexer_1_out
  Clock #(.highDuration(2), .lowDuration(2)) clock_1 (.out(clock_1_out));
  // Probe on register_1_q
  // Probe on register_1_q
  Register register_1 (.D(multiplexer_1_out), .en(1'b1), .clk(clock_1_out), .Q(register_1_q));  // open: clr
  // Probe on bancoderegistradores_1_b
  // Probe on Opcode
  ROM #(.addrWidth(4), .dataWidth(10)) MemoriaDeControle (
    .addr(Opcode), .data({ALUSrc, ALUOp, Branch, Jump, WriteReg, MemToReg, MemWrite, WriteR0}));
  // Probe on {Opcode, Resto}
  dual_port_ram dual_port_ram_1 (
    .addr(bancoderegistradores_1_b), .pc(register_1_q), .d(bancoderegistradores_1_a), .w(MemWrite),
    .instr({Opcode, Resto}), .data(dual_port_ram_1_data));
  // Probe on Resto
  // Probe on Opcode
  Multiplexer #(.width(8)) multiplexer_2 (
    .in0(ula_1_s), .in1(dual_port_ram_1_data), .out(multiplexer_2_out), .sel(MemToReg));
  // Probe on multiplexer_2_out
  Multiplexer #(.width(2)) multiplexer_3 (.in0(Resto[3:2]), .in1(2'b00), .out(multiplexer_3_out), .sel(WriteR0));
  // Probe on Resto[1:0]
  // Probe on multiplexer_2_out
  // Probe on multiplexer_3_out
  ExtensorSinal extensorsinal_2 (.A(Resto), .B(extensorsinal_2_b));
  // Probe on bancoderegistradores_1_a
  BancoDeRegistradores bancoderegistradores_1 (
    .Dados(multiplexer_2_out), .Clk(clock_1_out), .WriteReg(WriteReg), .RW(multiplexer_3_out),
    .RA(multiplexer_3_out), .RB(Resto[1:0]), .A(bancoderegistradores_1_a), .B(bancoderegistradores_1_b));
  // Probe on bancoderegistradores_1_a
  // Probe on bancoderegistradores_1_b
  Multiplexer #(.width(8)) multiplexer_4 (
    .in0(bancoderegistradores_1_b), .in1(extensorsinal_2_b), .out(multiplexer_4_out), .sel(ALUSrc));
  // Probe on extensorsinal_2_b
  // Probe on ALUOp
  ULA ula_1 (.A(bancoderegistradores_1_a), .B(multiplexer_4_out), .Funct(ALUOp), .Zero(ula_1_zero), .S(ula_1_s));

  // Notes on the sheet:
  //   contents of MemoriaDeControle (hex, n*v repeats v):
  //   120 310 10c 102 309 0 0 0 8 48 88 c8 108 148 188 1c8
endmodule

module BancoDeRegistradores (
  input  [7:0] Dados,
  input  Clk,
  input  WriteReg,
  input  [1:0] RW,
  input  [1:0] RA,
  input  [1:0] RB,
  output [7:0] A,
  output [7:0] B
);

  wire demultiplexer_1_out0, demultiplexer_1_out1, demultiplexer_1_out2, demultiplexer_1_out3;
  wire [7:0] register_1_q, register_2_q, register_3_q, register_4_q;

  Demultiplexer #(.select(2)) demultiplexer_1 (
    .out0(demultiplexer_1_out0), .out1(demultiplexer_1_out1), .out2(demultiplexer_1_out2),
    .out3(demultiplexer_1_out3), .in(WriteReg), .sel(RW));
  Register register_1 (.D(Dados), .en(demultiplexer_1_out0), .clk(Clk), .Q(register_1_q));  // open: clr
  Register register_2 (.D(Dados), .en(demultiplexer_1_out1), .clk(Clk), .Q(register_2_q));  // open: clr
  Register register_3 (.D(Dados), .en(demultiplexer_1_out2), .clk(Clk), .Q(register_3_q));  // open: clr
  Register register_4 (.D(Dados), .en(demultiplexer_1_out3), .clk(Clk), .Q(register_4_q));  // open: clr
  Multiplexer #(.select(2), .width(8)) multiplexer_1 (
    .in0(register_1_q), .in1(register_2_q), .in2(register_3_q), .in3(register_4_q), .out(A), .sel(RA));
  // Probe on A
  Multiplexer #(.select(2), .width(8)) multiplexer_2 (
    .in0(register_1_q), .in1(register_2_q), .in2(register_3_q), .in3(register_4_q), .out(B), .sel(RB));
endmodule

module ULA (
  input  [7:0] A,
  input  [7:0] B,
  input  [2:0] Funct,
  output Zero,
  output [7:0] S
);

  wire [7:0] D0, D1, D2, D3, D4, D5, D6, D7;

  assign D0 = ~B;  // NOT_Gate not_1, 8 bits wide
  assign D1 = A & B;  // AND_Gate and_1, 8 bits wide
  assign D2 = A | B;  // OR_Gate or_1, 8 bits wide
  assign D3 = A ^ B;  // XOR_Gate xor_1, 8 bits wide
  Adder adder_1 (.a(A), .b(B), .out(D4));  // open: cin, cout
  Subtractor subtractor_1 (.a(A), .b(B), .out(D5));  // open: bin, bout
  Shifter shifter_1 (.in(A), .\dist (B[2:0]), .out(D6));
  Shifter #(.shift("lr")) shifter_2 (.in(A), .\dist (B[2:0]), .out(D7));
  Comparator comparator_1 (.a(A), .b({8{1'b0}}), .eq(Zero));  // open: gt, lt
  // Probe on D6
  // Probe on D7
  Multiplexer #(.select(3), .width(8)) multiplexer_1 (
    .in0(D0), .in1(D1), .in2(D2), .in3(D3), .in4(D4), .in5(D5), .in6(D6), .in7(D7), .out(S), .sel(Funct));
endmodule

module ExtensorSinal (
  input  [3:0] A,
  output [7:0] B
);


  assign B = {{5{A[3]}}, A[2:0]};
endmodule

module ExtensorZero (
  input  [3:0] A,
  output [7:0] B
);


  assign B = {4'b0000, A};
endmodule
